# Fritzing sketch bipolar_stepper_L298N_driver (saved by Fritzing 0.8.7b)
breadboards: 2

parts:
  U1 = L298 [package=multiwatt15]
  Componente1 = Arduino Uno (Rev3)
  R1 = Resistor [tolerance=±5% resistance=2 package=THT]
  R2 = Resistor [tolerance=±5% resistance=2 package=THT]
  M1 = Stepper Motor - Bipolar
  VCC1 = 4 x AAA Battery Mount

nets:
  N1: U1.CSA, R1.Pin_0
  N2: U1.OUT1, M1.A
  N3: U1.OUT2, M1.C
  N4: U1.VS, VCC1.+
  N5: U1.IN1, Componente1.D8
  N6: U1.ENA, U1.VLS, U1.ENB, Componente1.5V
  N7: U1.IN2, Componente1.D9_PWM
  GND: U1.GND, Componente1.GND, R1.Pin_1, R2.Pin_0, VCC1.-
  N8: U1.IN3, Componente1.D10_PWM/SS
  N9: U1.IN4, Componente1.D11_PWM/MOSI
  N10: U1.OUT3, M1.B
  N11: U1.OUT4, M1.D
  N12: U1.CSB, R2.Pin_1
